# Fritzing sketch digitalPin_LED (saved by Fritzing 0.9.3b)
breadboards: 1

parts:
  Part1 = Adafruit Metro M4 AirLift Lite [part_number="Adafruit #4000"]
  R1 = Resistor [tolerance=±5% resistance=220 package=THT]
  LED1 = LED - 5mm [color="Red (633nm)" package="5 mm [THT]"]

nets:
  N1: Part1.GND, R1.Pin_1
  N2: Part1.D13, LED1.anode
  N3: R1.Pin_0, LED1.cathode

custom parts:
  Adafruit Metro M4 AirLift Lite: This is the Adafruit Metro M4 AirLift and Metro AirLift Lite, a Metro M4 with an ESP32 WiFi co-processor built in!
